// Digital circuit BW8cpu.dig as structural Verilog
module BW8cpu (
);

  wire a_dbus_a, a_dbus_l, a_lhs_a, a_rhs_a, addr_a, b_dbus_a, b_dbus_l, b_lhs_a, b_rhs_a, c_dbus_a,
       c_dbus_l, c_lhs_a, c_rhs_a, clr, d_dbus_a, d_dbus_l, d_lhs_a, d_rhs_a, dbus_a, dbus_l, ir_dbus_l,
       mem_dbus_a, mem_dbus_l, xfer_a, xfer_l;
  wire [7:0] clk, dbus, lhs, mbus, rhs;
  wire [15:0] addr_bus, xfer;

  control_unit Control_Unit ();  // open: nirq, opcode, flags, nreq, clk, nrst, dbus_assert, dbus_load, alu_op, xfer_assert, xfer_load, addr_assert, count, dec_sp, nbrk, nclk, noffset, rst, dbg
  // instruction_register Instruction_Register: pin names not known; wires that end beside it: clk, dbus, ir_dbus_l, clr
  alu alu_1 ();  // open: alu_op
  accumulator Accumulator (
    .a_dbus_load(a_dbus_l), .b_dbus_load(b_dbus_l), .a_dbus_assert(a_dbus_a), .b_dbus_assert(b_dbus_a),
    .a_lhs_assert(a_lhs_a), .b_lhs_assert(b_lhs_a), .a_rhs_assert(a_rhs_a), .b_rhs_assert(b_rhs_a),
    .dbus(dbus), .xfer(xfer), .clk(clk[0]), .clr(clr), .addr(addr_bus));  // open: addr_assert, xfer_load, reg_a, reg_b
  direct_page_register DP_Register ();  // open: dbus, clk, clr, assert_dp_addr, assert_t1_dbus, assert_t1_rhs, assert_dp_dbus, load_t1_dbus, load_dp_dbus, load_t2_dbus, assert_t_addr, assert_t2_dbus, assert_t2_lhs, t_inc, nclr, reg_dp, reg_t1, reg_t2, xfer, addr
  general_purpose_register C_Register (
    .DBUS_IN(clk), .CLK(c_dbus_l), .DBUS_LOAD(c_dbus_a), .DBUS_ASSERT(c_lhs_a), .LHS_ASSERT(c_rhs_a),
    .RHS_ASSERT(clr), .CLR(dbus[0]), .LHS(lhs), .RHS(rhs));  // open: DBUS_OUT
  memory_bridge Memory_Bridge (.dbus_assert(mem_dbus_a), .dbus_load(mem_dbus_l), .dbus(dbus), .mbus(mbus));
  general_purpose_register D_Register (
    .DBUS_IN(clk), .CLK(d_dbus_l), .DBUS_LOAD(d_dbus_a), .DBUS_ASSERT(d_lhs_a), .LHS_ASSERT(d_rhs_a),
    .RHS_ASSERT(clr), .CLR(dbus[0]), .LHS(lhs), .RHS(rhs));  // open: DBUS_OUT
  temp_register2 temp_register2_1 ();  // open: dbus, clk, clr, assert_dbus, assert_rhs, load_dbus, rhs, reg
  // bus_controller Bus_Controller: pin names not known; wires that end beside it: dbus_a, dbus_l, xfer_a, xfer_l, addr_a, a_dbus_a, b_dbus_a, c_dbus_a, d_dbus_a, mem_dbus_l, a_dbus_l, b_dbus_l, c_dbus_l, d_dbus_l, mem_dbus_a
  address_register Program_Counter ();  // open: xfer, clk, clr, xfer_load, addr_assert, xfer_assert, inc, dec, addr, reg
  address_register Stack_Pointer ();  // open: xfer, clk, clr, xfer_load, addr_assert, xfer_assert, inc, dec, addr, reg
  address_register X_Index ();  // open: xfer, clk, clr, xfer_load, addr_assert, xfer_assert, inc, dec, addr, reg
  address_register Y_Index ();  // open: xfer, clk, clr, xfer_load, addr_assert, xfer_assert, inc, dec, addr, reg
  // Pins of 1 and 8 bits meet at clk
  // Pins of 1 and 8 bits meet at dbus
endmodule
